# Fritzing sketch basic_electronics_2 (saved by Fritzing 0.9.3b)
stripboards: 1

parts:
  J2 = Basic Servo
  hc-sr1 = hc-sr04
  hc-sr2 = hc-sr04
  hc-sr3 = hc-sr04
  hc-sr4 = hc-sr04
  microSD_Transflash1 = SparkFun - microSD Transflash
  J1 = Basic Servo
  U4 = LIPO-2000mAh [package=lipo-2000]
  Part5 = Adafruit FONA 808 Breakout [part_number="Adafruit #2542"]
  Part6 = Adafruit LM3671 Buck Converter [part_number="Adafruit #2745"]
  DJI_ESC_30A1 = DJI 30A ESC
  DJI_ESC_30A2 = DJI 30A ESC
  U5 = 4-Channel 5v Relay Shield [package=relay-4ch5v10a]
  Part8 = Arduino Uno (Rev3) - ICSP
  ANT1 = Antenna  # not connected
  ANT2 = Antenna  # not connected
  R1 = Trimmer Potentiometer [maximum_resistance=10kΩ package=THT]

nets:
  GND: J2.gnd, J1.gnd
  VCC: J2.vcc, hc-sr1.VCC, hc-sr2.VCC, hc-sr3.VCC, hc-sr4.VCC, microSD_Transflash1.VCC, J1.vcc, Part5.Vio, DJI_ESC_30A1.PWR_OUT, DJI_ESC_30A2.PWR_OUT, U5.K2-On
  N1: hc-sr1.Trig, hc-sr1.Echo, Part8.A3
  GND_2: hc-sr1.GND, hc-sr2.GND, hc-sr3.GND, hc-sr4.GND, microSD_Transflash1.GND, Part5.GND, Part5.Key, DJI_ESC_30A1.GND, DJI_ESC_30A2.GND, U5.GND, Part8.GND
  N2: hc-sr2.Trig, hc-sr2.Echo, Part8.A1
  N3: hc-sr3.Trig, hc-sr3.Echo, Part8.A2
  N4: hc-sr4.Trig, hc-sr4.Echo, Part8.A0
  N5: microSD_Transflash1.DO, Part8.D12/MISO
  N6: microSD_Transflash1.SCK, Part8.D13/SCK
  N7: microSD_Transflash1.DI, Part8.ICSP_MOSI, Part8.D11_PWM/MOSI
  N8: microSD_Transflash1.CS, Part8.D10_PWM/SS
  N9: U4.+, Part6.VIN, U5.K1-In
  N10: U4.-, Part6.GND
  N11: Part5.Reset, Part8.D4
  N12: Part5.RXD, Part8.D2
  N13: Part5.TXD, Part8.D3_PWM
  3.3V: Part6.3.3V, U5.K2-In, U5.IN4, Part8.VIN
  N14: DJI_ESC_30A1.GROUND, DJI_ESC_30A2.GROUND
  +12V: DJI_ESC_30A1.+12V, DJI_ESC_30A2.+12V, U5.K1-On
  N15: DJI_ESC_30A2.DATA, Part8.D5_PWM
  N16: U5.IN1, Part8.D7
  N17: U5.IN2, Part8.D8
  N18: Part8.D6_PWM, R1.wiper

notes:
  5V Always On
  5V Switched
  1kOhm
  Reverser Y Harness

custom parts:
  Adafruit FONA 808 Breakout: Cellular + GPS tracking, all in one? Oh yes! Introducing Adafruit FONA 808 MiniGSM + GPS, an all-in-one cellular phone module with that lets you add location-tracking, voice, text, SMS and data to your project in an adorable little package.
  Adafruit LM3671 Buck Converter: Your power supply problems just got SUPER SOLVED! This 3.3V Buck Converter Breakout board is great for supplying power to low voltage circuits from a single Li-Ion cell battery or USB power. This chip provides up to 600-mA load current across the entire input voltage range of 3.5 to 5.5V. Great for your portable project, we made this "pin compatible" with the LM1117-3.3V TO-220 chip so you can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
  4-Channel 5v Relay Shield: 4 Channel 5v Relay Shield w. 2x SPD-06VDC-SD-C
