# Fritzing sketch basic_electronics_3 (saved by Fritzing 0.9.3b)
circuit board: 6cm x 8.46667cm
perfboards: 1

parts:
  Part5 = Adafruit FONA 808 Breakout [part_number="Adafruit #2542"]
  Part10 = Adafruit MicroSD card breakout board [part_number="Adafruit #254"]
  J3 = female pin header, 6 pins [form="♀ (female)"]
  J7 = Dagu DGServo 9g header (male) [package=THT]
  J8 = Dagu DGServo 9g header (male) [package=THT]
  J10 = male pin header, 3 pins [form="♂ (male)"]
  J11 = male pin header, 3 pins [form="♂ (male)"]
  J12 = male pin header, 3 pins [form="♂ (male)"]
  J13 = male pin header, 3 pins [form="♂ (male)"]
  J14 = male pin header, 3 pins [form="♂ (male)"]
  J9 = male pin header, 3 pins [form="♂ (male)"]
  LM1 = RioRand LM2596
  J15 = female pin header, 2 pins [form="♀ (female)"]
  J16 = female pin header, 2 pins [form="♀ (female)"]
  Part9 = Adafruit Metro Mini [part_number="Adafruit #2590"]

nets (from the pcb view):
  GND: Part5.GND, Part10.GND, J7.pulse, J8.pulse
  VCC: Part5.Vio, Part10.VCC, J3.pin6, J7.Vcc, J8.Vcc, J10.pin1, J11.pin1, J12.pin1, J13.pin1, J14.pin1, J9.pin1, J16.pin2
  N1: Part5.Reset, Part9.IO4
  N2: Part5.RXD, Part9.IO2
  N3: Part5.TXD, Part9.IO3
  N4: Part5.Key, LM1.Pin_3, Part9.GND
  N5: Part10.CLK, Part9.IO13
  N6: Part10.DO, Part9.IO12
  N7: Part10.DI, Part9.IO11
  N8: Part10.CS, Part9.IO10
  N9: J3.pin1, J10.pin2, J11.pin2, J12.pin2, J13.pin2, J14.pin2, J9.pin2, Part9.VIN
  N10: J3.pin2, Part9.IO7
  N11: J7.gnd, Part9.IO6
  N12: J8.gnd, Part9.IO5
  N13: J10.pin3, Part9.AD0
  N14: J11.pin3, Part9.AD2
  N15: J12.pin3, Part9.AD3
  N16: J13.pin3, Part9.AD4/SDA
  N17: J14.pin3, Part9.AD5/SCL
  N18: J9.pin3, Part9.AD1
  N19: LM1.Pin_0, J15.pin1
  N20: LM1.Pin_1, J15.pin2
  N21: LM1.Pin_2, J16.pin1

notes:
  7.2v in

custom parts:
  Adafruit FONA 808 Breakout: Cellular + GPS tracking, all in one? Oh yes! Introducing Adafruit FONA 808 MiniGSM + GPS, an all-in-one cellular phone module with that lets you add location-tracking, voice, text, SMS and data to your project in an adorable little package.
  Adafruit MicroSD card breakout board: Not just a simple breakout board, this microSD adapter goes the extra mile - designed for ease of use. Onboard 5v->3v regulator provides 150mA for power-hungry cards 3v level shifting means you can use this with ease on either 3v or 5v systems Uses a proper level shifting chip, not resistors: less problems, and faster read/write access Use 3 or 4 digital pins to read and write 2Gb+ of storage!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
  Adafruit Metro Mini: We sure love the ATmega328 here at Adafruit, and we use them a lot for our own projects. The processor has plenty of GPIO, Analog inputs, hardware UART SPI and I2C, timers and PWM galore - just enough for most simple projects. When we need to go small, we use a Pro Trinket 3V or 5V, but if you want to have USB-to-Serial built in, we reach for an Adafruit METRO Mini. METRO Mini is the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
