# Fritzing sketch basic_electronics_4 (saved by Fritzing 0.9.3b)
perfboards: 1

parts:
  Part1 = Adafruit Feather M0 Adalogger [part_number="Adafruit #2796"]
  LM1 = RioRand LM2596  # not connected
  Part2 = Adafruit FONA - Mini Cellular GSM Breakout  # not connected
  J2 = male pin header, 3 pins [form="♂ (male)"]
  J3 = male pin header, 3 pins [form="♂ (male)"]
  J4 = male pin header, 3 pins [form="♂ (male)"]
  J5 = male pin header, 3 pins [form="♂ (male)"]
  J6 = male pin header, 3 pins [form="♂ (male)"]
  J7 = male pin header, 3 pins [form="♂ (male)"]
  J8 = male pin header, 3 pins [form="♂ (male)"]
  J9 = male pin header, 3 pins [form="♂ (male)"]

nets:
  N1: Part1.GND, J2.pin3, J3.pin3, J4.pin3, J5.pin3, J6.pin3, J7.pin3, J8.pin1, J9.pin1
  N2: Part1.A5, J6.pin1
  N3: Part1.A4, J5.pin1
  N4: Part1.A3, J4.pin1
  N5: Part1.A2, J3.pin1
  N6: Part1.A1, J2.pin1
  N7: Part1.A0, J7.pin1
  N8: Part1.+3V3, J2.pin2, J3.pin2, J4.pin2, J5.pin2, J6.pin2, J7.pin2
  N9: J8.pin2, J9.pin2

custom parts:
  Adafruit Feather M0 Adalogger: This is the Adafruit Feather M0 Adalogger - our take on an 'all-in-one' Cortex M0 datalogger (or data-reader) with built in USB and battery charging. Its an Adafruit Feather M0 with a microSD holder ready to rock! We have other boards in the Feather family, check'em out here At the Feather M0's heart is an ATSAMD21G18 ARM Cortex M0 processor, clocked at 48 MHz and at 3.3V logic, the same one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
  Adafruit FONA - Mini Cellular GSM Breakout: An all-in-one cellular phone module that lets you add voice, text, SMS and GPRS data to your project. Quad-band 850/900/1800/1900MHz - connect onto any global GSM network with any 2G SIM. Includes an onboard LiPoly battery charging circuitry so you can take your project on the go. Also works as an FM radio receiver.
