# Fritzing sketch pir-breakout (saved by Fritzing 0.9.3b)
perfboards: 1

parts:
  IC1 = MCP23017 I2C I/O Expander
  J1 = shrouded pin header, 10 pins [form="♂ (shrouded male)"]
  J2 = male pin header, 3 pins [form="♂ (male)"]
  J3 = male pin header, 3 pins [form="♂ (male)"]
  J4 = male pin header, 3 pins [form="♂ (male)"]
  J5 = male pin header, 3 pins [form="♂ (male)"]
  R1 = Resistor [tolerance=±5% resistance=220 package=THT]

nets:
  N1: IC1.VDD, J1.pin10, J2.pin3, J3.pin1, J4.pin1, J5.pin3
  N2: IC1.VSS, J1.pin9, J2.pin1, J4.pin3, J5.pin1
  N3: IC1.SCL, J1.pin6
  N4: IC1.SDA, J1.pin7
  N5: IC1.A0, IC1.A1, IC1.A2, R1.Pin_1
  N6: IC1.RESET, R1.Pin_0
  N7: IC1.INTA, J1.pin8
  N8: IC1.GPA0, J5.pin2
  N9: IC1.GPA1, J2.pin2
  N10: IC1.GPA2, J3.pin2
  N11: IC1.GPA3, J4.pin2

custom parts:
  MCP23017 I2C I/O Expander: The MCP23017 uses two i2c pins (these can be shared with other i2c devices), and in exchange gives you 16 general purpose pins. You can set each of 16 pins to be input, output, input with a pullup or open drain. There's even the ability to get an interrupt via an external pin when any of the inputs change so you don't have to keep polling the chip.
