# Fritzing sketch pir-breakout1 (saved by Fritzing 0.9.3b)
perfboards: 1

parts:
  IC1 = MCP23017 I2C I/O Expander
  J1 = shrouded pin header, 10 pins [form="♂ (shrouded male)"]
  J2 = male pin header, 3 pins [form="♂ (male)"]  # not connected
  J3 = male pin header, 3 pins [form="♂ (male)"]  # not connected
  J4 = male pin header, 3 pins [form="♂ (male)"]  # not connected
  J5 = male pin header, 3 pins [form="♂ (male)"]  # not connected
  R1 = Resistor [tolerance=±5% resistance=220 package=THT]  # not connected

nets:
  N1: IC1.VDD, J1.pin10
  N2: IC1.VSS, J1.pin9
  N3: IC1.SCL, J1.pin6
  N4: IC1.SDA, J1.pin7

custom parts:
  MCP23017 I2C I/O Expander: The MCP23017 uses two i2c pins (these can be shared with other i2c devices), and in exchange gives you 16 general purpose pins. You can set each of 16 pins to be input, output, input with a pullup or open drain. There's even the ability to get an interrupt via an external pin when any of the inputs change so you don't have to keep polling the chip.
